// Digital circuit state_char.dig as structural Verilog
module state_char (
  input  [7:0] D,
  output next,
  output done
);

  wire not_1_out;

  not not_1 (not_1_out, D[0]);
  and and_1 (next, not_1_out, D[1]);
  and and_2 (done, not_1_out, D[2]);
endmodule
